# Fritzing sketch Sunshine (saved by Fritzing 0.9.3b)
circuit board: 4.84389cm x 2.81649cm
breadboards: 1

parts:
  Power_plug1 = Power plug
  S1 = Momentary Switch [package=ksa_sealed_tac_switch]
  U1 = ESP8266 WiFi Module [part_number=ESP8266]
  S4 = Toggle Switch [package=THT]
  J1 = female pin header, 2 pins [form="♀ (female)"]
  J2 = female pin header, 2 pins [form="♀ (female)"]
  J3 = female pin header, 2 pins [form="♀ (female)"]
  C1 = Capacitor Polarized [package=cpol-radial-100uf-25v]
  C5 = Capacitor Polarized [package=cpol-radial-10uf-25v]
  U3 = Voltage Regulator LM1117 [package=sot223]
  C3 = Capacitor [package=0805]
  C4 = Capacitor [package=0805]
  Q1 = 2N7000 FET N-Channel [part_number=2N7000 package=TO92]

nets:
  GND: Power_plug1.GND, S1.1, S1.2, U1.GND, S4.L1, J3.pin1, J3.pin2, C1.-, C5.-, U3.ADJ, C3.1, C4.1, Q1.source
  N1: Power_plug1.VCC, J1.pin2, C1.+, U3.IN, C3.2
  N2: S1.4, U1.RST
  N3: U1.RXD, J2.pin1
  N4: U1.VCC, U1.CH_PD, C5.+, U3.OUT, C4.2
  N5: U1.GPIO_0, S4.COM
  N6: U1.GPIO_2, Q1.gate
  N7: U1.TXD, J2.pin2
  N8: J1.pin1, Q1.drain

custom parts:
  ESP8266 WiFi Module: Generic WiFi Module based on the ESP8266 with onboard PCB antenna and UART communications
  2N7000 FET N-Channel: A 2N7000 MOSFET N-Channel Transistor
